// Logisim project 8051.circ as structural Verilog
module main (
  input  Reset,
  input  [7:0] in_2
);

  wire CLK_out, clock_1_out, controlunit_1_p4, controlunit_1_p5, controlunit_1_p8, controlunit_1_p9,
       controlunit_1_p10, controlunit_1_p11, controlunit_1_p12, decoder_1_out0, decoder_1_out1,
       decoder_1_out2, decoder_1_out3, decoder_1_out4, decoder_1_out5;
  wire [3:0] controlled_buffer_1_out, controlunit_1_p6, controlunit_1_p7;
  wire [7:0] ALU_Buffer1_q, ALU_Buffer2_q, ALU_Output_q, alu_v2_1_accumulator, ControlUnitDataBuffer_q,
       multiplexer_1_out, RegisterA_q, RegisterB_q;

  // NoConnect on decoder_1_out5
  Decoder #(.select(4)) decoder_1 (
    .out0(decoder_1_out0), .out1(decoder_1_out1), .out2(decoder_1_out2), .out3(decoder_1_out3),
    .out4(decoder_1_out4), .out5(decoder_1_out5), .sel(controlunit_1_p6), .en(controlunit_1_p9));  // open: out6, out7, out8, out9, out10, out11, out12, out13, out14, out15
  Clock clock_1 (.out(clock_1_out));
  // ControlUnit controlunit_1: pin names not known; wires that end beside it: Reset, in_2, clock_1_out, controlunit_1_p4, controlunit_1_p5, controlunit_1_p6, controlunit_1_p7, controlunit_1_p8, controlunit_1_p9, controlunit_1_p10, controlunit_1_p11, controlunit_1_p12
  // NoConnect on decoder_1_out4
  Clock CLK (.out(CLK_out));
  Register ALU_Buffer1 (.D(multiplexer_1_out), .en(decoder_1_out0), .clk(CLK_out), .Q(ALU_Buffer1_q), .clr(Reset));
  Register ALU_Buffer2 (.D(multiplexer_1_out), .en(decoder_1_out1), .clk(CLK_out), .Q(ALU_Buffer2_q), .clr(Reset));
  Register RegisterA (.D(multiplexer_1_out), .en(decoder_1_out2), .clk(CLK_out), .Q(RegisterA_q), .clr(Reset));
  Register RegisterB (.D(multiplexer_1_out), .en(decoder_1_out3), .clk(CLK_out), .Q(RegisterB_q), .clr(Reset));
  Register ALU_Output (.D(alu_v2_1_accumulator), .en(1'b1), .clk(CLK_out), .Q(ALU_Output_q), .clr(Reset));
  Multiplexer #(.select(4), .width(8)) multiplexer_1 (
    .in2(RegisterA_q), .in3(RegisterB_q), .in4(ALU_Output_q), .out(multiplexer_1_out),
    .sel(controlled_buffer_1_out));  // open: in0, in1, in5, in6, in7, in8, in9, in10, in11, in12, in13, in14, in15
  assign controlled_buffer_1_out = controlunit_1_p11 ? controlunit_1_p6 : 4'bz;  // Controlled_Buffer controlled_buffer_1
  ALU_v2 alu_v2_1 (
    .Buffer1(ALU_Buffer1_q), .Buffer2(ALU_Buffer2_q), .Opcode(controlunit_1_p7),
    .Accumulator(alu_v2_1_accumulator));  // open: OverflowIn, AuxiliaryCarryIn, CarryIn, ALU_OutputAux, CarryFlag, ZeroFlag, SignFlag, AuxiliaryCarryFlag, OverflowFlag
  Register ControlUnitDataBuffer (
    .D(multiplexer_1_out), .en(controlunit_1_p11), .clk(CLK_out), .Q(ControlUnitDataBuffer_q), .clr(Reset));
  assign multiplexer_1_out = controlunit_1_p9 ? ControlUnitDataBuffer_q : 8'bz;  // Controlled_Buffer controlled_buffer_2

  // Notes on the sheet:
  //   RegisterSelectBus
  //   registerAddressForInput
  //   Data Bus
  //   registerAddressForOutput
endmodule

module ALU_v2 (
  input  OverflowIn,
  input  AuxiliaryCarryIn,
  input  CarryIn,
  input  [7:0] Buffer1,
  input  [7:0] Buffer2,
  input  [3:0] Opcode,
  output [7:0] Accumulator,
  output [7:0] ALU_OutputAux,
  output CarryFlag,
  output ZeroFlag,
  output SignFlag,
  output AuxiliaryCarryFlag,
  output OverflowFlag
);

  wire adder_4_cout, adder_5_cout, adder_6_cout, adder_7_cout, adder_8_cout, adder_10_cout, comparator_1_lt,
       comparator_2_lt, comparator_3_lt, comparator_5_eq, comparator_5_gt, nor_1_out, or_1_out, xor_1_out,
       xor_2_out, xor_4_out;
  wire [6:0] adder_9_out, negator_2_out;
  wire [7:0] adder_1_out, adder_2_out, adder_3_out, adder_4_out, adder_5_out, adder_6_out, and_1_out,
       and_2_out, and_3_out, bit_extender_3_out, bit_extender_4_out, divider_1_out, divider_1_rem,
       multiplier_1_out, negator_1_out, or_2_out, shifter_1_out, shifter_2_out, undriven, xor_3_out;
  wire [15:0] bit_extender_1_out, bit_extender_2_out;
  wire [15:8] multiplier_1_out_2;

  Adder adder_1 (.a({8{1'b0}}), .b(Buffer2), .out(adder_1_out), .cin(CarryIn));  // open: cout
  Negator negator_1 (.in(adder_1_out), .out(negator_1_out));
  assign bit_extender_1_out = {{8{Buffer2[7]}}, Buffer2};  // Bit_Extender bit_extender_1
  assign bit_extender_2_out = {{8{Buffer1[7]}}, Buffer1};  // Bit_Extender bit_extender_2
  Comparator #(.mode("unsigned")) comparator_1 (.a(Buffer1), .b(Buffer2), .lt(comparator_1_lt));  // open: gt, eq
  Adder adder_2 (.a(8'h1), .b(Buffer1), .out(adder_2_out));  // open: cin, cout
  Adder adder_3 (.a({8{1'b1}}), .b(Buffer1), .out(adder_3_out));  // open: cin, cout
  Adder adder_4 (.a(Buffer1), .b(Buffer2), .out(adder_4_out), .cout(adder_4_cout));  // open: cin
  Adder adder_5 (.a(Buffer1), .b(Buffer2), .out(adder_5_out), .cin(CarryIn), .cout(adder_5_cout));
  Adder adder_6 (.a(Buffer1), .b(negator_1_out), .out(adder_6_out), .cout(adder_6_cout));  // open: cin
  Multiplier #(.width(16)) multiplier_1 (
    .a(bit_extender_1_out), .b(bit_extender_2_out), .out({multiplier_1_out_2, multiplier_1_out}));  // open: cin, cout
  Adder #(.width(4)) adder_7 (.a(Buffer1[3:0]), .b(Buffer2[3:0]), .cout(adder_7_cout));  // open: out, cin
  Adder #(.width(4)) adder_8 (.a(Buffer1[3:0]), .b(Buffer2[3:0]), .cin(CarryIn), .cout(adder_8_cout));  // open: out
  xor xor_1 (xor_1_out, CarryIn, adder_4_cout);
  Divider divider_1 (.a(Buffer1), .b(Buffer2), .out(divider_1_out), .rem(divider_1_rem));  // open: upper
  Comparator #(.mode("unsigned"), .width(4)) comparator_2 (
    .a(Buffer1[3:0]), .b(Buffer2[3:0]), .lt(comparator_2_lt));  // open: gt, eq
  xor xor_2 (xor_2_out, CarryIn, adder_5_cout);
  or or_1 (or_1_out, multiplier_1_out_2[8], multiplier_1_out_2[9], multiplier_1_out_2[10], multiplier_1_out_2[11], multiplier_1_out_2[12], multiplier_1_out_2[13], multiplier_1_out_2[14], multiplier_1_out_2[15]);
  nor nor_1 (nor_1_out, Buffer2[0], Buffer2[1], Buffer2[2], Buffer2[3], Buffer2[4], Buffer2[5], Buffer2[6], Buffer2[7]);
  Shifter #(.shift("rr")) shifter_1 (.in(Buffer1), .\dist (3'b001), .out(shifter_1_out));
  Shifter #(.shift("rl")) shifter_2 (.in(Buffer1), .\dist (3'b001), .out(shifter_2_out));
  // NoConnect on undriven
  assign or_2_out = Buffer1 | Buffer2;  // OR_Gate or_2, 8 bits wide
  assign and_1_out = Buffer1 & Buffer2;  // AND_Gate and_1, 8 bits wide
  assign xor_3_out = Buffer1 ^ Buffer2;  // XOR_Gate xor_3, 8 bits wide
  Comparator comparator_3 (.a(Buffer1), .b(Buffer2), .lt(comparator_3_lt));  // open: gt, eq
  Comparator #(.mode("unsigned")) comparator_4 (.a(Buffer1), .b(Buffer2), .eq(ZeroFlag), .lt(SignFlag));  // open: gt
  Adder #(.width(7)) adder_9 (.a({7{1'b0}}), .b(Buffer2[6:0]), .out(adder_9_out), .cin(CarryIn));  // open: cout
  Multiplexer #(.select(4), .width(8)) multiplexer_1 (
    .in0(adder_2_out), .in1(adder_3_out), .in2(adder_4_out), .in3(adder_5_out), .in4(adder_6_out),
    .in5(multiplier_1_out), .in6(divider_1_out), .in7(or_2_out), .in8(and_1_out), .in9(xor_3_out),
    .in10(undriven), .in11(shifter_1_out), .in12(shifter_1_out), .in13(shifter_2_out), .in14(shifter_2_out),
    .in15(Buffer1), .out(Accumulator), .sel(Opcode));
  Adder #(.width(7)) adder_10 (.a(Buffer1[6:0]), .b(negator_2_out), .cout(adder_10_cout));  // open: out, cin
  Negator #(.width(7)) negator_2 (.in(adder_9_out), .out(negator_2_out));
  Comparator #(.mode("unsigned"), .width(4)) comparator_5 (
    .a(Opcode), .b(4'b0101), .gt(comparator_5_gt), .eq(comparator_5_eq));  // open: lt
  xor xor_4 (xor_4_out, adder_6_cout, adder_10_cout);
  assign bit_extender_3_out = {{7{comparator_5_eq}}, comparator_5_eq};  // Bit_Extender bit_extender_3
  assign bit_extender_4_out = {{7{comparator_5_gt}}, comparator_5_gt};  // Bit_Extender bit_extender_4
  Multiplexer #(.select(4)) multiplexer_2 (
    .in0(CarryIn), .in1(CarryIn), .in2(adder_4_cout), .in3(adder_5_cout), .in4(comparator_1_lt), .in5(1'b0),
    .in6(1'b0), .in7(CarryIn), .in8(CarryIn), .in9(CarryIn), .in10(comparator_3_lt), .in12(Buffer1[0]),
    .in14(Buffer1[7]), .out(CarryFlag), .sel(Opcode));  // open: in11, in13, in15
  Multiplexer #(.select(4)) multiplexer_3 (
    .in0(CarryIn), .in1(CarryIn), .in2(adder_7_cout), .in3(adder_8_cout), .in4(comparator_2_lt),
    .in5(AuxiliaryCarryIn), .in6(AuxiliaryCarryIn), .in7(AuxiliaryCarryIn), .in8(AuxiliaryCarryIn),
    .in9(AuxiliaryCarryIn), .in10(AuxiliaryCarryIn), .out(AuxiliaryCarryFlag), .sel(Opcode));  // open: in11, in12, in13, in14, in15
  Multiplexer #(.select(4)) multiplexer_4 (
    .in0(CarryIn), .in1(CarryIn), .in2(xor_1_out), .in3(xor_2_out), .in4(xor_4_out), .in5(or_1_out),
    .in6(nor_1_out), .in7(OverflowIn), .in8(OverflowIn), .in9(OverflowIn), .in10(OverflowIn),
    .out(OverflowFlag), .sel(Opcode));  // open: in11, in12, in13, in14, in15
  assign and_2_out = bit_extender_3_out & multiplier_1_out_2;  // AND_Gate and_2, 8 bits wide
  assign and_3_out = bit_extender_4_out & divider_1_rem;  // AND_Gate and_3, 8 bits wide
  assign ALU_OutputAux = and_2_out | and_3_out;  // OR_Gate or_3, 8 bits wide

  // Notes on the sheet:
  //   ACC ->
  //   2. operand ->
  //   cin
  //   A
  //   B
endmodule

module ControlUnit (
  input  [7:0] InstructionLine,
  input  LockAluOpcode,
  input  Finish,
  input  [3:0] ConditionSatisfied,
  input  CarryFlag,
  input  ZeroFlag,
  input  CarryFlagCheck,
  input  ZeroFlagCheck,
  input  [3:0] ConditionNotSatisfied,
  output [7:0] EffectiveAddress,
  output IncrementPC,
  output [3:0] RegisterAddress,
  output [3:0] ALU_Opcode,
  output MemoryRead,
  output RegisterStore,
  output MemoryWrite,
  output RegisterLoad,
  output MemoryEnable
);

  wire clock_1_out, multiplexer_1_out, or_1_out, undriven, undriven_2;
  wire [3:0] and_1_out, and_2_out, bit_extender_1_out, OpcodeToALU_Opcode_out, or_2_out;

  PLA #(.in_width(8), .out_width(4), .\table ("00000011 1011 # rr\n00010011 1100 # rrc\n00100011 1101 # rl\n00110011 1110 # rlc\n0000x1xx 0000 # inc\n0001x1xx 0001 # dec\n0010x1xx 0010 # add\n0011x1xx 0011 # addc\n0100xx10 0111 # orl\n0101xx1x 1000 # anl\n1001x1xx 0100 # subb\n11011xxx 1010 # compare (djnz)")) OpcodeToALU_Opcode (
    .in(InstructionLine), .out(OpcodeToALU_Opcode_out));
  Register #(.width(4)) ALU_OpcodeRegister (
    .D(OpcodeToALU_Opcode_out), .en(LockAluOpcode), .clk(clock_1_out));  // open: Q, clr
  Clock clock_1 (.out(clock_1_out));
  // NoConnect on undriven
  // NoConnect on undriven_2
  Multiplexer #(.select(2)) multiplexer_1 (
    .in0(undriven), .in1(CarryFlag), .in2(ZeroFlag), .in3(undriven_2), .out(multiplexer_1_out),
    .sel({ZeroFlagCheck, CarryFlagCheck}));
  assign bit_extender_1_out = {{3{multiplexer_1_out}}, multiplexer_1_out};  // Bit_Extender bit_extender_1
  or or_1 (or_1_out, CarryFlagCheck, ZeroFlagCheck);
  assign and_1_out = ConditionSatisfied & bit_extender_1_out;  // AND_Gate and_1, 4 bits wide
  assign and_2_out = ~bit_extender_1_out & ConditionNotSatisfied;  // AND_Gate and_2, 4 bits wide
  assign or_2_out = and_1_out | and_2_out;  // OR_Gate or_2, 4 bits wide
  SequenceGenerator sequencegenerator_1 (
    .Reset(Finish), .LoadData(or_1_out), .Data(or_2_out));  // open: Clock, Completed, Value
endmodule

module SequenceGenerator (
  input  Reset,
  input  LoadData,
  input  Clock,
  input  [3:0] Data,
  output Completed,
  output [3:0] Value
);

  Counter #(.max('h5), .ongoal("stay"), .width(4)) counter_1 (
    .clr(Reset), .load(LoadData), .up(1'b1), .count(1'b1), .clk(Clock), .D(Data), .carry(Completed), .Q(Value));
endmodule
